// Logisim project template.circ as structural Verilog: 1 circuit, main circuit main
module main (
);

  wire clock_1_out;
  wire [31:0] counter_1_q;

  TTY #(.rows(48), .cols(120)) tty_1 (.clk(clock_1_out));  // open: data, we, clr
  Clock clock_1 (.out(clock_1_out));
  Counter #(.width(32), .max('hffffffff)) counter_1 (
    .Q(counter_1_q), .clk(clock_1_out));  // open: load, D, count, carry, clr
endmodule
